# Fritzing sketch Untitled Sketch (saved by Fritzing 0.9.1b)
circuit board: 8.46667cm x 5.64444cm
breadboards: 1

parts:
  IC1 = Dual Op-Amp [package=dip08]
  R5 = Resistor [tolerance=±5% resistance=100k package=THT]
  R6 = Resistor [tolerance=±5% resistance=100k package=THT]
  R7 = Resistor [tolerance=±5% resistance=100k package=THT]
  R8 = Resistor [tolerance=±5% resistance=100k package=THT]
  C1 = Ceramic Capacitor [capacitance=1pF voltage=50V package="0805 [SMD, multilayer]"]
  C2 = Ceramic Capacitor [capacitance=1pF voltage=50V package="0805 [SMD, multilayer]"]
  C3 = Ceramic Capacitor [capacitance=1pF voltage=50V package="0805 [SMD, multilayer]"]
  C4 = Ceramic Capacitor [capacitance=1pF voltage=50V package="0805 [SMD, multilayer]"]
  C5 = Electrolytic Capacitor [capacitance=2.2µF voltage=50V package="200 mil [THT, electrolytic]"]
  R13 = Resistor [tolerance=±5% resistance=100k package=THT]
  R9 = Resistor [tolerance=±5% resistance=100k package=THT]
  R11 = Resistor [tolerance=±5% resistance=100k package=THT]
  R10 = Resistor [tolerance=±5% resistance=100k package=THT]
  R12 = Resistor [tolerance=±5% resistance=100k package=THT]
  C6 = Electrolytic Capacitor [capacitance=2.2µF voltage=50V package="200 mil [THT, electrolytic]"]
  C7 = Electrolytic Capacitor [capacitance=22µF voltage=50V package="200 mil [THT, electrolytic]"]
  R14 = Resistor [tolerance=±5% resistance=1M package=THT]
  U1 = 3.5mm Audio Jack [package=audio-jack-3.5mm-smd]
  U2 = 3.5mm Audio Jack [package=audio-jack-3.5mm-smd]  # not connected
  U3 = 3.5mm Audio Jack [package=audio-jack-3.5mm-smd]  # not connected
  R109 = Resistor [tolerance=±5% resistance=100k package=THT]
  R114 = Resistor [tolerance=±5% resistance=1M package=THT]
  R113 = Resistor [tolerance=±5% resistance=100k package=THT]
  R100 = Resistor [tolerance=±5% resistance=100k package=THT]
  IC2 = Dual Op-Amp [package=dip08]
  C105 = Electrolytic Capacitor [capacitance=2.2µF voltage=50V package="200 mil [THT, electrolytic]"]

nets:
  N1: IC1.A_OUT, R9.Pin_1, R10.Pin_0
  N2: IC1.A_-IN, R5.Pin_0, R5.Pin_1, R6.Pin_0, R6.Pin_1, C1.1, C2.1, R9.Pin_0
  N3: IC1.A_+IN, IC1.B_+IN, R11.Pin_1, R12.Pin_0, C7.+, IC2.A_+IN, IC2.B_+IN
  GND: IC1.A_V-, R11.Pin_0, C6.-, C7.-, R14.Pin_1, U1.SLEEVE, R114.Pin_1, IC2.A_V-
  N4: IC1.B_-IN, R13.Pin_0, R10.Pin_1
  N5: IC1.B_OUT, C5.+
  N6: R7.Pin_0, R7.Pin_1, R8.Pin_0, R8.Pin_1, C3.1, C4.1, IC2.A_-IN
  N7: C5.-, R14.Pin_0, U1.RIGHT
  N8: R12.Pin_1, C6.+
  N9: U1.LEFT, C105.-
  N10: R109.Pin_1, R100.Pin_0, IC2.A_OUT
  N11: R113.Pin_0, R100.Pin_1, IC2.B_-IN
  N12: IC2.B_OUT, C105.+
